# Fritzing sketch work-mode (saved by Fritzing 0.9.10b)
breadboards: 1

parts:
  元件1 = Arduino Nano 33 IoT
  M1 = DC Motor [voltage_(max)=6V voltage_(min)=3V]
  元件2 = FC-28 Soil Hygrometer Module
  元件3 = FC-28 Soil Hygrometer Module - Probe

nets:
  N1: 元件1.D2, M1.pin_2
  GND: 元件1.GND, M1.pin_1, 元件2.GND
  N2: 元件1.A0, 元件2.AO
  3V3: 元件1.3V3, 元件2.VCC
  N3: 元件2.POS, 元件3.POS
  N4: 元件2.NEG, 元件3.NEG

custom parts:
  Arduino Nano 33 IoT: The Arduino Nano 33 IoT is a small, complete, and breadboard-friendly board based on the Arm® Cortex®-M0 32-bit SAMD21. It has onboard WiFi and Bluetooth® connectivity through a u-blox NINA-W10 chipset. Secure communication is ensured through the Microchip® ECC608 crypto chip. It also has 6-axis LSM6DS3 IMU.
  FC-28 Soil Hygrometer Module: The FC-28 is a soil hygrometer module that uses the Texas Instruments LM393 comparator chip to provide an analog measurement of soil humidity. The digital output is high when soil moisture is over a certain threshold, as determined by adjusting the potentiometer.
  FC-28 Soil Hygrometer Module - Probe: The FC-28 is a soil hygrometer module that uses the Texas Instruments LM393 comparator chip to provide an analog measurement of soil humidity.
